// Logisim project MemInstruc.circ as structural Verilog: 1 circuit, main circuit main
module main (
  input  [31:0] instrucao,
  input  [31:0] pc
);

  ROM #(.addrWidth(24), .dataWidth(32)) rom_1 (.addr(pc[25:2]), .data(instrucao));
endmodule
