// Logisim project d09.circ as structural Verilog: 1 circuit, main circuit main
module main (
);

  wire clock_1_out, ucprincipal_1_alusrc, ucprincipal_1_regwrite;
  wire [2:0] decodificador_1_funct3;
  wire [4:0] decodificador_1_rd, decodificador_1_rs1, decodificador_1_rs2;
  wire [5:0] decodificador_1_opcode;
  wire [31:0] bancoregistradores_1_ld1, bancoregistradores_1_ld2, decodificador_1_imediato,
       multiplexer_1_out, undriven;

  Clock clock_1 (.out(clock_1_out));
  decodificador decodificador_1 (
    .Instrucao(undriven), .rd(decodificador_1_rd), .opcode(decodificador_1_opcode),
    .funct3(decodificador_1_funct3), .rs1(decodificador_1_rs1), .rs2(decodificador_1_rs2),
    .Imediato(decodificador_1_imediato));
  ucPrincipal ucprincipal_1 (
    .in_1(decodificador_1_opcode), .ALUSrc(ucprincipal_1_alusrc), .RegWrite(ucprincipal_1_regwrite));  // open: MemToReg, MemRead, Branch, MemWrite
  bancoRegistradores bancoregistradores_1 (
    .WR(decodificador_1_rd), .RegWrite(ucprincipal_1_regwrite), .LR1(decodificador_1_rs1),
    .LR2(decodificador_1_rs2), .clk(clock_1_out), .LD1(bancoregistradores_1_ld1),
    .LD2(bancoregistradores_1_ld2));  // open: WD
  Multiplexer #(.width(32)) multiplexer_1 (
    .in0(bancoregistradores_1_ld2), .in1(decodificador_1_imediato), .out(multiplexer_1_out),
    .sel(ucprincipal_1_alusrc));
  ULA ula_1 (
    .B(multiplexer_1_out), .ALUControl(decodificador_1_funct3), .A(bancoregistradores_1_ld1));  // open: sZero, Result
endmodule
